// Logisim project And.circ as structural Verilog: 1 circuit, main circuit main
module main (
  input  a,
  input  b,
  output out
);

  wire nand_1_out;

  nand nand_1 (nand_1_out, a, b);
  not not_1 (out, nand_1_out);

  // Notes on the sheet:
  //   And Gate
endmodule
