// Logisim project Computer.circ as structural Verilog: 1 circuit, main circuit main
module main (
);

  wire Reset_out, undriven, undriven_2, undriven_3;
  wire [15:0] counter_1_q, demultiplexer_1_out0, demultiplexer_1_out1, multiplexer_1_out, ram_1_data,
       register_1_q, register_2_q, rom_1_data;

  RAM #(.addrWidth(16), .dataWidth(16), .bus("asynch")) ram_1 (
    .addr(register_1_q), .data(ram_1_data), .ld(demultiplexer_1_out1[0]));  // open: sel, clr
  ROM #(.addrWidth(16), .dataWidth(16)) rom_1 (.addr(counter_1_q), .data(rom_1_data));  // open: sel
  Demultiplexer #(.width(16), .enable("false")) demultiplexer_1 (
    .out0(demultiplexer_1_out0), .out1(demultiplexer_1_out1), .in(rom_1_data), .sel(rom_1_data[0]));
  Register #(.width(16)) register_1 (
    .D(demultiplexer_1_out0), .Q(register_1_q), .clk(demultiplexer_1_out1[0]));  // open: en, clr
  Register #(.width(16)) register_2 (.D(demultiplexer_1_out0), .Q(register_2_q));  // open: en, clk, clr
  Button Reset (.out(Reset_out));
  Multiplexer #(.width(16), .enable("false")) multiplexer_1 (
    .in0(register_1_q), .in1(ram_1_data), .out(multiplexer_1_out), .sel(demultiplexer_1_out1[0]));
  Counter #(.width(16), .max('hffff)) counter_1 (
    .load(undriven), .D(register_1_q), .Q(counter_1_q), .clr(Reset_out));  // open: count, carry, clk
  ROM #(.addrWidth(16), .dataWidth(16)) rom_2 (.data(demultiplexer_1_out0));  // open: addr, sel
  _7_Segment_Display #(.active("false")) u_7_segment_display_1 (
    .f(demultiplexer_1_out1[0]), .a(undriven_3), .b(undriven_2), .e(undriven));  // open: g, d, c, dp
  // Pins of 1 and 16 bits meet at demultiplexer_1_out1
  // Pins of 1 and 16 bits meet at rom_1_data

  // Notes on the sheet:
  //   Orange= control bus
  //   Add
  //   add
  //   RAM
  //   d3(load in)
  //   ROM
  //   RAM in
  //   RAM out (M)
  //   out
  //   c
  //   c[0]
  //   Address Register
  //   d1
  //   d2
  //   Data Register
  //   c[4]
  //   load
  //   in A
  //   D
  //   in 1
  //   in 2
  //   A/M
  //   PC
  //   ALU
  //   ALU Fn
  //   out
  //   ALU out
  //   Ng
  //   Zr
  //   JUMP CHIP
endmodule
