// Logisim project Dmux.circ as structural Verilog: 1 circuit, main circuit main
module main (
  input  In,
  input  sel,
  output a,
  output b
);

  wire Notsel_out;

  not Notsel (Notsel_out, sel);
  and and_1 (a, In, Notsel_out);
  and and_2 (b, In, sel);

  // Notes on the sheet:
  //   inAndNotsel
  //   inAndsel
endmodule
