// Logisim project Mux.circ as structural Verilog: 3 circuits, main circuit main
module main (
  input  a,
  input  b,
  input  selctor,
  output out
);

  wire and_1_out, and_2_out, and_3_out, not_1_out, not_2_out, not_3_out;

  not not_1 (not_1_out, b);
  not not_2 (not_2_out, selctor);
  not not_3 (not_3_out, a);
  and and_1 (and_1_out, a, b);
  and and_2 (and_2_out, a, not_1_out, not_2_out);
  and and_3 (and_3_out, not_3_out, b, selctor);
  or or_1 (out, and_1_out, and_2_out, and_3_out);

  // Notes on the sheet:
  //   a
  //   b
  //   a
  //   Notb
  //   Nots
  //   Nota
  //   b
  //   s
  //   aAndb
  //   aNotbAndNots
  //   NotabAnds
endmodule

module mux (
  input  a,
  input  b,
  input  selctor,
  output x
);

  wire and_1_out, and_2_out, not_1_out;

  not not_1 (not_1_out, selctor);
  and and_1 (and_1_out, b, selctor);
  and and_2 (and_2_out, a, not_1_out);
  or or_1 (x, and_1_out, and_2_out);
endmodule

module Mux_Revised (
  input  a,
  input  b,
  input  sel,
  output Out
);

  wire and_1_out, and_2_out, not_1_out;

  not not_1 (not_1_out, sel);
  and and_1 (and_1_out, a, not_1_out);
  and and_2 (and_2_out, b, sel);
  or or_1 (Out, and_1_out, and_2_out);

  // Notes on the sheet:
  //   Notsel
  //   aAndNotsel
  //   bAndsel
endmodule
