// Logisim project NOT.circ as structural Verilog: 1 circuit, main circuit main
module main (
  input  a,
  output out_2
);

  not nand_1 (out_2, a);  // NAND_Gate

  // Notes on the sheet:
  //   b
  //   NOT using NAND
endmodule
