// Logisim project Or.circ as structural Verilog: 1 circuit, main circuit main
module main (
  input  a,
  input  b,
  input  a_2,
  input  b_2,
  input  a_3,
  input  b_3,
  output out,
  output out_2,
  output out_3
);

  wire and_1_out, and_2_out, and_3_out, not_1_out, not_2_out, not_3_out, not_4_out;

  not not_1 (not_1_out, a);
  not not_2 (not_2_out, b);
  and and_1 (and_1_out, a_3, a_3);
  and and_2 (and_2_out, b_3, b_3);
  not not_3 (not_3_out, a_2);
  not not_4 (not_4_out, b_2);
  and and_3 (and_3_out, not_1_out, not_2_out);
  nand nand_1 (out_2, not_3_out, not_4_out);
  nand nand_2 (out_3, and_1_out, and_2_out);
  not not_5 (out, and_3_out);

  // Notes on the sheet:
  //   OR GATE
endmodule
