// Logisim project Xor.circ as structural Verilog: 1 circuit, main circuit main
module main (
  input  a,
  input  b,
  output out
);

  wire and_1_out, and_2_out, not_a_out, not_b_out;

  not not_a (not_a_out, a);
  not not_b (not_b_out, b);
  and and_1 (and_1_out, not_a_out, b);
  and and_2 (and_2_out, a, not_b_out);
  or or_1 (out, and_1_out, and_2_out);

  // Notes on the sheet:
  //   notaAndb
  //   aAndNotb
endmodule
